# Fritzing sketch SmartWiper (saved by Fritzing 0.8.7b)

parts:
  Part1 = Arduino Pro Mini v13
  Part2 = Triple Axis Accelerometer Breakout - ADXL335
  Part3 = Bluetooth Mate Silver
  Part_4 = FTDI Basic Programmer
  Batt = LIPO-110mAh [package=lipo-110]

nets:
  N1: Part1.DTR, Part_4.DTR
  N2: Part1.D0/TX, Part_4.RXI
  N3: Part1.D1/RX, Part_4.TXO
  VCC: Part1.VCC, Part2.ST, Part2.VCC, Part3.VCC, Part_4.POWER, Batt.+
  GND: Part1.GND, Part2.GND, Part3.GND, Part_4.CTS, Part_4.GND, Batt.-
  N4: Part1.A2, Part2.ZOUT
  N5: Part1.A1, Part2.YOUT
  N6: Part1.A0, Part2.XOUT
  N7: Part1.D3_PWM, Part3.RX_5V
  N8: Part1.D2, Part3.TX_5V
